// Logisim project mini-arquitetura.circ as structural Verilog: 1 circuit, main circuit mini-arquitetura
module mini_arquitetura (
  input  RESET,
  output [2:0] RD,
  output [3:0] REG0,
  output [3:0] REG1,
  output [3:0] REG2,
  output [3:0] REG3,
  output [3:0] REG4,
  output [3:0] REG5,
  output [3:0] REG6,
  output [3:0] REG7,
  output [2:0] RF1,
  output [2:0] RF2,
  output [2:0] OPCODE
);

  wire BEQ_out, BNE_out, clock_1_out, decodificador_1_d0, decodificador_1_d1, decodificador_1_d2,
       decodificador_1_d3, decodificador_1_d4, decodificador_1_d5, decodificador_1_d6, decodificador_1_d7,
       JMP_out, not_1_out, not_2_out, not_3_out, not_4_out, not_5_out, or_1_out, ula_1_equal;
  wire [3:0] main_1_out_5, multiplexer_1_out, multiplexer_2_out, ram_1_data, ula_1_resultado_op;

  Clock clock_1 (.out(clock_1_out));
  or or_1 (or_1_out, JMP_out, BEQ_out, BNE_out);
  and JMP (JMP_out, OPCODE[2], not_1_out, not_2_out);
  and BEQ (BEQ_out, ula_1_equal, OPCODE[2], OPCODE[1], not_3_out);
  and BNE (BNE_out, not_4_out, not_5_out, OPCODE[2], OPCODE[0]);
  contador_main main_1 (.RESET(RESET), .LOAD(or_1_out), .DATA(ram_1_data), .out_5(main_1_out_5), .CLOCK(clock_1_out));
  not not_1 (not_1_out, OPCODE[1]);
  not not_2 (not_2_out, OPCODE[0]);
  not not_3 (not_3_out, OPCODE[0]);
  not not_4 (not_4_out, ula_1_equal);
  not not_5 (not_5_out, OPCODE[1]);
  RAM #(.addrWidth(4), .dataWidth(16)) ram_1 (
    .addr(main_1_out_5), .data({OPCODE, RD, RF1, RF2, ram_1_data}), .clk(clock_1_out));  // open: sel, ld, clr
  ULA ula_1 (
    .IMEDIATO_000(ram_1_data), .ENTRADA_Y(multiplexer_2_out), .ENTRADA_X(multiplexer_1_out), .S1(OPCODE[1]),
    .S0(OPCODE[0]), .RESULTADO_OP(ula_1_resultado_op), .EQUAL(ula_1_equal));
  DECODIFICADOR decodificador_1 (
    .SELECT(RD), .D0(decodificador_1_d0), .D1(decodificador_1_d1), .D2(decodificador_1_d2),
    .D3(decodificador_1_d3), .D4(decodificador_1_d4), .D5(decodificador_1_d5), .D6(decodificador_1_d6),
    .D7(decodificador_1_d7));
  Multiplexer #(.select(3), .width(4)) multiplexer_1 (
    .in0(REG0), .in1(REG1), .in2(REG2), .in3(REG3), .in4(REG4), .in5(REG5), .in6(REG6), .in7(REG7),
    .out(multiplexer_1_out), .sel(RF1));  // open: en
  Multiplexer #(.select(3), .width(4)) multiplexer_2 (
    .in0(REG0), .in1(REG1), .in2(REG2), .in3(REG3), .in4(REG4), .in5(REG5), .in6(REG6), .in7(REG7),
    .out(multiplexer_2_out), .sel(RF2));  // open: en
  banco_registradores_main main_2 (
    .Reset(RESET), .En_Reg0(decodificador_1_d0), .En_Reg1(decodificador_1_d1), .En_Reg2(decodificador_1_d2),
    .En_Reg3(decodificador_1_d3), .DATA(ula_1_resultado_op), .En_Reg4(decodificador_1_d4),
    .En_Reg5(decodificador_1_d5), .En_Reg6(decodificador_1_d6), .En_Reg_7(decodificador_1_d7),
    .Clock(clock_1_out), .Out_Reg0(REG0), .Out_Reg1(REG1), .Out_Reg2(REG2), .Out_Reg3(REG3), .Out_Reg4(REG4),
    .Out_Reg5(REG5), .Out_Reg6(REG6), .Out_Reg7(REG7), .WRITE(OPCODE[2]));
endmodule
